// Logisim project somador.circ as structural Verilog: 4 circuits, main circuit Meio Somador
module Meio_Somador (
  input  A0,
  input  B0,
  input  B0_2,
  output S0,
  output S0_2,
  output S0_3
);

  xor xor_1 (S0, A0, B0);
  and and_1 (S0_3, A0, B0);
  and and_2 (S0_3, A0, B0);

  assign B0_2 = B0;
  assign S0_2 = S0;

  // Notes on the sheet:
  //   Meio somador
  //   Meio somador
endmodule

module Somador_Completo (
  input  A0,
  input  B0,
  input  Ci0,
  output S0,
  output S0_2
);

  wire meio_somador_1_s0_2, meio_somador_1_s0_3, meio_somador_3_s0_3;

  Meio_Somador meio_somador_1 (.A0(A0), .B0_2(B0), .S0_2(meio_somador_1_s0_2), .S0_3(meio_somador_1_s0_3));
  Meio_Somador meio_somador_2 (.A0(A0), .B0_2(B0), .S0_2(meio_somador_1_s0_2), .S0_3(meio_somador_1_s0_3));
  Meio_Somador meio_somador_3 (.A0(meio_somador_1_s0_2), .B0_2(Ci0), .S0_2(S0), .S0_3(meio_somador_3_s0_3));
  or or_1 (S0_2, meio_somador_3_s0_3, meio_somador_1_s0_3);

  // Notes on the sheet:
  //   Somador Completo
endmodule

module Somador_de_4_bits (
  input  [3:0] A,
  input  [3:0] A_2,
  input  Carry_out,
  output [3:0] S,
  output Over_flow,
  output Carry_out_2
);

  wire somador_completo_1_s0_2, somador_completo_2_s0_2, somador_completo_3_s0_2;
  wire [3:0] undriven;

  Somador_Completo somador_completo_1 (
    .A0(A[0]), .B0(undriven[0]), .Ci0(Carry_out), .S0(S[0]), .S0_2(somador_completo_1_s0_2));
  Somador_Completo somador_completo_2 (
    .A0(A[1]), .B0(undriven[1]), .Ci0(somador_completo_1_s0_2), .S0(S[1]), .S0_2(somador_completo_2_s0_2));
  Somador_Completo somador_completo_3 (
    .A0(A[2]), .B0(undriven[2]), .Ci0(somador_completo_2_s0_2), .S0(S[2]), .S0_2(somador_completo_3_s0_2));
  Somador_Completo somador_completo_4 (
    .A0(A[3]), .B0(undriven[3]), .Ci0(somador_completo_3_s0_2), .S0(S[3]), .S0_2(Carry_out_2));
  xor xor_1 (Over_flow, somador_completo_3_s0_2, Carry_out_2);

  assign A_2 = A;

  // Notes on the sheet:
  //   +
endmodule

module main (
  input  Carry_In,
  input  [3:0] A,
  input  [3:0] A_2,
  input  [3:0] B,
  output Over_Flow,
  output Carry_Out,
  output Over_Flow_2,
  output Carry_Out_2
);

  wire displaydecoder_1_p3, displaydecoder_1_p5, displaydecoder_1_p6, displaydecoder_1_p7,
       displaydecoder_1_p8, displaydecoder_1_p9, displaydecoder_1_p10, displaydecoder_1_p11,
       displaydecoder_2_p2, displaydecoder_2_p3, displaydecoder_2_p4, displaydecoder_2_p5,
       displaydecoder_3_p1, displaydecoder_3_p2, displaydecoder_4_p2, displaydecoder_4_p3,
       displaydecoder_4_p4, displaydecoder_4_p5, displaydecoder_5_p1, displaydecoder_5_p2,
       displaydecoder_5_p3;

  // DisplayDecoder displaydecoder_1: pin names not known; wires that end beside it: A_2, A, displaydecoder_1_p3, displaydecoder_1_p3, displaydecoder_1_p5, displaydecoder_1_p6, displaydecoder_1_p7, displaydecoder_1_p8, displaydecoder_1_p9, displaydecoder_1_p10, displaydecoder_1_p11
  // Somador_de_4_bits somador_de_4_bits_1: pin names not known; wires that end beside it: displaydecoder_1_p3, B, Carry_In, Carry_Out, Carry_Out_2, Over_Flow, Over_Flow_2
  // Somador_de_4_bits somador_de_4_bits_2: pin names not known; wires that end beside it: Carry_Out_2
  // DisplayDecoder displaydecoder_2: pin names not known; wires that end beside it: B, displaydecoder_2_p2, displaydecoder_2_p3, displaydecoder_2_p4, displaydecoder_2_p5
  // DisplayDecoder displaydecoder_3: pin names not known; wires that end beside it: displaydecoder_3_p1, displaydecoder_3_p2
  _7_Segment_Display u_7_segment_display_1 (
    .g(displaydecoder_1_p11), .f(displaydecoder_1_p10), .a(displaydecoder_1_p5), .b(displaydecoder_1_p6),
    .e(displaydecoder_1_p9), .d(displaydecoder_1_p8), .c(displaydecoder_1_p7));  // open: dp
  _7_Segment_Display u_7_segment_display_2 (
    .g(displaydecoder_3_p1), .f(displaydecoder_3_p2), .a(displaydecoder_2_p2), .b(displaydecoder_2_p3),
    .e(displaydecoder_3_p1), .d(displaydecoder_2_p5), .c(displaydecoder_2_p4));  // open: dp
  // DisplayDecoder displaydecoder_4: pin names not known; wires that end beside it: Over_Flow, displaydecoder_4_p2, displaydecoder_4_p3, displaydecoder_4_p4, displaydecoder_4_p5
  // DisplayDecoder displaydecoder_5: pin names not known; wires that end beside it: displaydecoder_5_p1, displaydecoder_5_p2, displaydecoder_5_p3
  _7_Segment_Display u_7_segment_display_3 (
    .g(displaydecoder_5_p3), .f(displaydecoder_5_p2), .a(displaydecoder_4_p2), .b(displaydecoder_4_p3),
    .e(displaydecoder_5_p1), .d(displaydecoder_4_p5), .c(displaydecoder_4_p4));  // open: dp

  // Notes on the sheet:
  //   Calculadora de 4 bits
  //   +
endmodule
